# Fritzing sketch Click_to_Go_receiver (saved by Fritzing 0.9.2b)
breadboards: 1

parts:
  IC1 = L293D [package=THT]
  M2 = DC Motor
  Part1 = Arduino Uno (Rev3) - ICSP
  BAT1 = BC9VPC [package=bc9vpc]
  M3 = DC Motor
  NRF24L2 = NRF24L01
  VCC1 = Battery  # not connected

nets:
  N1: IC1.Enable_1, IC1.Enable_2, Part1.D4
  N2: IC1.In_1, Part1.D5_PWM
  N3: IC1.Out_1_(_Controlled_by_Enable_1_), M2.pin_2
  N4: IC1.0V, BAT1.V-
  N5: IC1.Out_2_(_Controlled_by_Enable_1_), M2.pin_1
  N6: IC1.In_2, Part1.D3_PWM
  N7: IC1.+Vmotor, IC1.+V, BAT1.V+
  N8: IC1.In_3, Part1.D7
  N9: IC1.Out_3_(_Controlled_by_Enable_2_), M3.pin_1
  N10: IC1.Out_4_(_Controlled_by_Enable_2_), M3.pin_2
  N11: IC1.In_4, Part1.D6_PWM
  GND: Part1.A4/SDA, Part1.GND, NRF24L2.GND
  N12: Part1.ICSP_MOSI, Part1.D11_PWM/MOSI, NRF24L2.MOSI
  N13: Part1.D9_PWM, NRF24L2.CE
  N14: Part1.D10_PWM/SS, NRF24L2.CSN
  N15: Part1.D12/MISO, NRF24L2.MISO
  N16: Part1.D13/SCK, NRF24L2.SCK
  3V3: Part1.3V3, NRF24L2.VCC

custom parts:
  NRF24L01: NRF24L01 module
