# Fritzing sketch Click_to_Go_transmitter (saved by Fritzing 0.9.2b)

parts:
  Part1 = Arduino Uno (Rev3) - ICSP
  NRF24L2 = NRF24L01

nets:
  N1: Part1.ICSP_MOSI, Part1.D11_PWM/MOSI, NRF24L2.MOSI
  N2: Part1.D9_PWM, NRF24L2.CE
  N3: Part1.D10_PWM/SS, NRF24L2.CSN
  N4: Part1.D12/MISO, NRF24L2.MISO
  N5: Part1.D13/SCK, NRF24L2.SCK
  3V3: Part1.3V3, NRF24L2.VCC
  GND: Part1.GND, NRF24L2.GND

custom parts:
  NRF24L01: NRF24L01 module
